# Fritzing sketch TimeTrafficLight (saved by Fritzing 0.9.5d)
breadboards: 1

parts:
  Rpi = Raspberry Pi Zero
  part = Resistor [tolerance=±5% resistance=100 package=THT]
  part_2 = LED - 5mm [color="Red (633nm)" package="5 mm [THT]"]
  part_3 = Resistor [tolerance=±5% resistance=100 package=THT]
  part_4 = LED - 5mm [color="Yellow (574nm)" package="5 mm [THT]"]
  part_5 = LED - 5mm [color="Green (555nm)" package="5 mm [THT]"]
  part_6 = Resistor [tolerance=±5% resistance=100 package=THT]

nets:
  N1: Rpi.pin_6, Rpi.pin_39, part.Pin_1, part_3.Pin_1, part_6.Pin_1
  N2: Rpi.pin_33, part_5.anode
  N3: Rpi.pin_35, part_4.anode
  N4: Rpi.pin_37, part_2.anode
  N5: part.Pin_0, part_2.cathode
  N6: part_3.Pin_0, part_4.cathode
  N7: part_5.cathode, part_6.Pin_0
